# Fritzing sketch ProyectoRiego (saved by Fritzing 0.9.3b)
breadboards: 1

parts:
  R1 = Resistor [tolerance=±5% resistance=220 package=THT]
  D1 = Rectifier Diode [part_number=1N4001 package="300 mil [THT]"]
  Q1 = NPN-Transistor [package="TO92 [THT]"]
  M1 = DC Motor
  Componente1 = Arduino Uno (Rev3)
  DHT1 = Humidity and Temperature Sensor DHT11
  부품3 = FC-28 Soil Hygrometer Module
  부품4 = FC-28 Soil Hygrometer Module - Probe
  S2 = Round Pushbutton
  R2 = Photocell (LDR) [package=THT]
  R3 = Resistor [tolerance=±5% resistance=220 package=THT]
  D2 = Rectifier Diode [part_number=1N4001 package="300 mil [THT]"]
  Q2 = NPN-Transistor [package="TO92 [THT]"]
  부품5 = FC-28 Soil Hygrometer Module - Probe
  부품6 = FC-28 Soil Hygrometer Module
  부품7 = FC-28 Soil Hygrometer Module - Probe
  부품8 = FC-28 Soil Hygrometer Module
  S3 = Round Pushbutton
  S4 = Pushbutton [package="[THT]"]
  R4 = Resistor [tolerance=±5% resistance=10k package=THT]
  R5 = Resistor [tolerance=±5% resistance=10k package=THT]
  LED1 = RGB LED (com. anode, rbg) [package="5 mm [THT]"]
  R6 = Resistor [tolerance=±5% resistance=1 package=THT]
  R7 = Resistor [tolerance=±5% resistance=1 package=THT]
  M2 = DC Motor
  J1 = Piezo Speaker
  R8 = Resistor [tolerance=±5% resistance=1 package=THT]

nets:
  N1: R1.Pin_0, Componente1.D6_PWM
  N2: R1.Pin_1, D2.cathode, Q2.B
  N3: D1.cathode, Q1.E, M1.pin_2
  VCC: D1.anode, M1.pin_1, Componente1.5V, DHT1.GND_2, 부품3.VCC, R2.pin_0, D2.anode, 부품6.VCC, 부품8.VCC, S4.Pin_3, S4.Pin_4, M2.pin_1
  N4: Q1.B, R3.Pin_0
  GND: Q1.C, Componente1.GND, DHT1.Data-signal, 부품3.GND, S2.leg1, Q2.C, 부품6.GND, 부품8.GND, S3.leg1, R4.Pin_1, R5.Pin_0, J1.pin1
  N5: Componente1.A2, R2.pin_1, R5.Pin_1
  N6: Componente1.A3, 부품6.AO
  N7: Componente1.A4/SDA, 부품8.AO
  N8: Componente1.A5/SCL, 부품3.AO
  N9: Componente1.D8, S4.Pin_1, S4.Pin_2, R4.Pin_0
  N10: Componente1.D10_PWM/SS, J1.pin2
  N11: Componente1.D11_PWM/MOSI, R6.Pin_1
  N12: Componente1.D12/MISO, R7.Pin_1
  N13: Componente1.D13/SCK, R8.Pin_1
  N14: Componente1.D2, DHT1.GND_1
  N15: Componente1.D4, S3.leg0
  N16: Componente1.D5_PWM, R3.Pin_1
  N17: Componente1.D7, S2.leg0
  N18: 부품3.POS, 부품4.POS
  N19: 부품3.NEG, 부품4.NEG
  N20: Q2.E, M2.pin_2
  N21: 부품5.POS, 부품8.POS
  N22: 부품5.NEG, 부품8.NEG
  N23: 부품6.POS, 부품7.POS
  N24: 부품6.NEG, 부품7.NEG
  N25: LED1.common_anode, R8.Pin_0
  N26: LED1.blue_cathode, R7.Pin_0
  N27: LED1.green_cathode, R6.Pin_0

notes:
  5V Line
  GND Line
  Analog Input Line
  Digital Input Line
  Digital Output Line
  Sistema de riego

custom parts:
  Humidity and Temperature Sensor DHT11: Digital relative humidity & temperature sensor DHT11
  FC-28 Soil Hygrometer Module: The FC-28 is a soil hygrometer module that uses the Texas Instruments LM393 comparator chip to provide an analog measurement of soil humidity. The digital output is high when soil moisture is over a certain threshold, as determined by adjusting the potentiometer.
  FC-28 Soil Hygrometer Module - Probe: The FC-28 is a soil hygrometer module that uses the Texas Instruments LM393 comparator chip to provide an analog measurement of soil humidity.
